# Fritzing sketch Laser Tank Circuit DIagrams (saved by Fritzing 0.9.3b)

parts:
  Part1 = Arduino Motor Shield (Rev3)
  Part2 = Arduino Uno (Rev3)
  Nano1 = Arduino Nano v2.3
  M1 = DC Motor
  M2 = DC Motor
  VCC1 = Battery block 9V
  J1 = Basic Servo
  LED1 = LED - 5mm [color="Red (633nm)" package="5 mm [THT]"]
  C1 = Electrolytic Capacitor [capacitance=4.7µF voltage=50V package="0605 [SMD, electrolytic]"]
  R1 = PHOTOCELL [package=photocell-kit]
  R3 = PHOTOCELL [package=photocell-kit]
  R4 = PHOTOCELL [package=photocell-kit]
  R5 = Resistor [tolerance=±5% resistance=430 package=THT]
  R6 = PHOTOCELL [package=photocell-kit]
  R7 = PHOTOCELL [package=photocell-kit]
  R8 = PHOTOCELL [package=photocell-kit]
  R9 = Resistor [tolerance=±5% resistance=430 package=THT]
  Part3 = NRF24L01+ Breakout Board
  C2 = Electrolytic Capacitor [capacitance=2.2µF package="0807 [SMD, electrolytic]"]
  S1 = SPST Switch [package=switch-spdt-smd]
  VCC2 = 4 x AAA Battery Mount
  Part4 = Thumb Joystick
  Part5 = Thumb Joystick
  Part6 = NRF24L01+ Breakout Board

nets:
  N1: Part1.A3, R8.P$2, R9.Pin_1
  N2: Part1.A4, R4.P$2, R5.Pin_1
  N3: Part1.A5, LED1.cathode
  N4: Part1.D9/BreakeA, Part3.CE
  N5: Part1.D10_PWM, Part3.CS
  N6: Part1.D11_PWM/B, Part2.D2
  N7: Part1.D12/DirA, Part2.D4
  N8: Part1.D13/DirB, Part2.D6_PWM
  N9: Part1.D2, Part2.D11_PWM/MOSI, Part3.MOSI
  N10: Part1.D4, Part2.D12/MISO, Part3.MISO
  N11: Part1.D6_PWM, Part2.D13/SCK, Part3.SCK
  N12: Part1.B-, M1.pin_2
  N13: Part1.B+, M1.pin_1
  N14: Part1.A-, M2.pin_2
  N15: Part1.A+, M2.pin_1
  N16: Part1.VMOT, VCC1.+
  GND: Part1.GND, VCC1.-, J1.gnd, LED1.anode, C1.+, R9.Pin_0, Part3.GND, C2.-
  N17: Part1.D5_PWM, J1.pulse
  5V: Part1.5V, J1.vcc, C1.-, R1.P$1, R6.P$1
  3V3: Part1.3V3, Part3.VCC, C2.+
  GND_2: Nano1.GND, VCC2.-, Part4.GND, Part5.GND, Part6.GND
  N18: Nano1.D9, Part6.CE
  N19: Nano1.D10, Part6.CS
  N20: Nano1.D11, Part6.MOSI
  N21: Nano1.D12, Part6.MISO
  N22: Nano1.D13, Part6.SCK
  3V3_2: Nano1.3V3, Part6.VCC
  N23: Nano1.A3, Part5.HORZ
  N24: Nano1.A2, Part5.VERT
  N25: Nano1.A1, Part4.HORZ
  N26: Nano1.A0, Part4.VERT
  VCC: Nano1.+5V, Part4.VCC, Part5.VCC
  N27: Nano1.VIN, S1.P
  N28: R1.P$2, R3.P$1
  N29: R3.P$2, R4.P$1
  N30: R6.P$2, R7.P$1
  N31: R7.P$2, R8.P$1
  N32: S1.S, VCC2.+

notes:
  I used a 9.6v rechargable battery
  except where otherwise noted, the motor shield pins are directly linked to the corresponding pins on the arduino
  This LED is a 3mw red laser diode
  TANK MAIN
  TANK CONTROLLER
